# Fritzing sketch ARduino and TM1637 (saved by Fritzing 0.9.2b)

parts:
  Grove1 = Grove 4 Digit Display
  Part1 = Arduino Uno (Rev3)

nets:
  GND: Grove1.GND, Part1.GND
  VCC: Grove1.VCC, Part1.5V
  N1: Grove1.DIO, Part1.D2
  N2: Grove1.CLK, Part1.D3_PWM

// code stored in the sketch: TM1637ino.ino
#include <TM1637Display.h>

const int CLK = 3; //Set the CLK pin connection to the display
const int DIO = 2; //Set the DIO pin connection to the display

int numCounter = 0;

TM1637Display display(CLK, DIO);  //set up the 4-Digit Display.

void setup()
{
  display.setBrightness(0x0a);  //set the diplay to maximum brightness
}


void loop()
{
  for(numCounter = 0; numCounter < 1000; numCounter++)  //Iterate numCounter
  {
    display.showNumberDec(numCounter); //Display the numCounter value;
    delay(1000);
  }
}
