# Fritzing sketch Arduino and L298 (saved by Fritzing 0.9.2b)
breadboards: 1

parts:
  Part1 = Arduino Uno (Rev3)
  M1 = DC Motor
  S1 = Round Pushbutton
  U1 = L298 [package=multiwatt15]

nets:
  N1: Part1.D9_PWM, U1.ENA
  GND: Part1.GND, S1.leg1, U1.CSA, U1.GND, U1.CSB
  N2: Part1.D2, S1.leg0
  N3: Part1.D3_PWM, U1.IN1
  N4: Part1.D4, U1.IN2
  5V: Part1.5V, U1.VLS
  N5: M1.pin_1, U1.OUT1
  N6: M1.pin_2, U1.OUT2
  12V: U1.VS
