# Fritzing sketch Arduino and PCF8574 (saved by Fritzing 0.9.2b)

parts:
  Part1 = Arduino Uno (Rev3)
  U1 = PCF8574 [package="DIP16 [THT]"]
  R1 = Resistor [tolerance=±5% resistance=330 package=THT]
  LED1 = LED - 5mm [color="Red (633nm)" package="5 mm [THT]"]
  R2 = Resistor [tolerance=±5% resistance=330 package=THT]
  LED2 = LED - 5mm [color="Red (633nm)" package="5 mm [THT]"]
  R3 = Resistor [tolerance=±5% resistance=330 package=THT]
  R4 = Resistor [tolerance=±5% resistance=330 package=THT]
  LED3 = LED - 5mm [color="Red (633nm)" package="5 mm [THT]"]
  LED4 = LED - 5mm [color="Red (633nm)" package="5 mm [THT]"]
  R5 = Resistor [tolerance=±5% resistance=330 package=THT]
  R6 = Resistor [tolerance=±5% resistance=220 package=THT]
  LED5 = LED - 5mm [color="Red (633nm)" package="5 mm [THT]"]
  LED6 = LED - 5mm [color="Red (633nm)" package="5 mm [THT]"]
  R7 = Resistor [tolerance=±5% resistance=220 package=THT]
  R8 = Resistor [tolerance=±5% resistance=220 package=THT]
  LED7 = LED - 5mm [color="Red (633nm)" package="5 mm [THT]"]
  LED8 = LED - 5mm [color="Red (633nm)" package="5 mm [THT]"]

nets:
  N1: Part1.A4/SDA, U1.SDA
  N2: Part1.A5/SCL, U1.SCL
  5V: Part1.5V, U1.VCC
  GND: Part1.GND, U1.A0, U1.A1, U1.A3, U1.GND, LED1.cathode, LED2.cathode, LED3.cathode, LED4.cathode, LED5.cathode, LED6.cathode, LED7.cathode, LED8.cathode
  N3: U1.P0, R1.Pin_0
  N4: U1.P1, R2.Pin_0
  N5: U1.P2, R3.Pin_0
  N6: U1.P3, R4.Pin_0
  N7: U1.P4, R5.Pin_0
  N8: U1.P5, R6.Pin_0
  N9: U1.P6, R8.Pin_0
  N10: U1.P7, R7.Pin_0
  N11: R1.Pin_1, LED1.anode
  N12: R2.Pin_1, LED2.anode
  N13: R3.Pin_1, LED4.anode
  N14: R4.Pin_1, LED3.anode
  N15: R5.Pin_1, LED6.anode
  N16: R6.Pin_1, LED5.anode
  N17: R7.Pin_1, LED8.anode
  N18: R8.Pin_1, LED7.anode
