# Fritzing sketch Arduino to atttiny2313 (saved by Fritzing 0.9.2b)
circuit board: 8.46667cm x 5.64444cm
breadboards: 1

parts:
  U1 = ATTINY2313 [package=dip]
  Part1 = Arduino Uno (Rev3)

nets:
  N1: U1.PA2_(RESET/dW), Part1.D10_PWM/SS
  GND: U1.GND, Part1.GND
  N2: U1.PB5_(MOSI/DI/SDA/PCINT5), Part1.D11_PWM/MOSI
  N3: U1.PB6_(MISO/DO/PCINT6), Part1.D12/MISO
  N4: U1.PB7_(UCSK/SCK/PCINT7), Part1.D13/SCK
  VCC: U1.VCC, Part1.5V

custom parts:
  ATTINY2313: Atmel 20-pin 2kb flash uC
