# Fritzing sketch Arduino to atttiny44 (saved by Fritzing 0.9.2b)
breadboards: 1

parts:
  Part1 = Arduino Uno (Rev3)
  U1 = ATTiny84 [package=dip]
  C1 = Electrolytic Capacitor [capacitance=10µF voltage=16V package="100 mil [THT, electrolytic]"]

nets:
  N1: Part1.D10_PWM/SS, U1.pin4
  N2: Part1.D11_PWM/MOSI, U1.pin7
  N3: Part1.D12/MISO, U1.pin8
  N4: Part1.D13/SCK, U1.pin9
  N5: Part1.GND, U1.pin14, C1.-
  N6: Part1.RESET, C1.+
  N7: Part1.5V, U1.pin1

custom parts:
  ATTiny84: Atmel ATTiny84 processor. 8 ADC pins, 4 PWM pins. Available in either 10MHz or 20MHz. The last 2 pin numbers refer to arduino. D6 = Arduino 6, A6 = Arduino A6 example: PA6 (SDA/MOSI/OC1A/DI/AD6/PCINT6/D6/A6) NOTE: This part is diagrammed to suit the MIT HLT ATTiny84 core at https://github.com/damellis/attiny/
