# Fritzing sketch Arduino to atttiny85 (saved by Fritzing 0.9.2b)
circuit board: 8.46667cm x 5.64444cm
breadboards: 1

parts:
  Part1 = Arduino Uno (Rev3)
  U1 = attiny85 [package=dip]

nets:
  N1: Part1.D10_PWM/SS, U1.Pin_1
  N2: Part1.D11_PWM/MOSI, U1.Pin_5
  N3: Part1.D12/MISO, U1.Pin_6
  N4: Part1.D13/SCK, U1.Pin_7
  N5: Part1.5V, U1.Pin_8
  N6: Part1.GND, U1.Pin_4
