# Fritzing sketch Barebones No PSU (saved by Fritzing 0.9.2b)
circuit board: 3.91601cm x 4.86192cm
breadboards: 1

parts:
  U1 = atmega328 [package=dip]
  R1 = Resistor [tolerance=±5% resistance=220 package=THT]
  J1 = female pin header, 5 pins [form="♀ (female)"]
  J2 = female pin header, 4 pins [form="♀ (female)"]
  J3 = female pin header, 5 pins [form="♀ (female)"]
  J4 = female pin header, 6 pins [form="♀ (female)"]
  C1 = Ceramic Capacitor [capacitance=10pF package="200 mil [THT, multilayer]"]
  C2 = Ceramic Capacitor [capacitance=10pF package="200 mil [THT, multilayer]"]
  XTAL1 = Crystal [frequency="16 Mhz" package=THT]
  J5 = Screw terminal - 2 pins [package=THT]

nets:
  N1: U1.RESET, R1.Pin_1
  N2: U1.D0_(RX), J1.pin1
  N3: U1.D1_(TX), J1.pin2
  N4: U1.D2, J1.pin3
  N5: U1.D3_(PWM), J1.pin4
  N6: U1.D4, J1.pin5
  5V: U1.VCC, U1.AVCC, U1.AREF, R1.Pin_0, J5.pin2
  GND: U1.GND, C1.0, C2.0, J5.pin1
  N7: U1.XLAT1, C1.1, XTAL1.pin_0
  N8: U1.XLAT2, C2.1, XTAL1.pin_1
  N9: U1.D5_(PWM), J2.pin1
  N10: U1.D6_(PWM), J2.pin2
  N11: U1.D7, J2.pin3
  N12: U1.D8, J2.pin4
  N13: U1.D9_(PWM), J3.pin5
  N14: U1.D10_(PWM), J3.pin4
  N15: U1.D11_(PWM), J3.pin3
  N16: U1.D12, J3.pin2
  N17: U1.D13, J3.pin1
  N18: U1.A0, J4.pin6
  N19: U1.A1, J4.pin5
  N20: U1.A2, J4.pin4
  N21: U1.A3, J4.pin3
  N22: U1.A4, J4.pin2
  N23: U1.A5, J4.pin1
