# Fritzing sketch IR and RGB LED (saved by Fritzing 0.9.0b)

parts:
  Part1 = Arduino Uno (Rev3)
  LED1 = RGB LED (com. anode, rbg) [package="5 mm [THT]"]
  R1 = Resistor [tolerance=±5% resistance=220 package=THT]
  R2 = Resistor [tolerance=±5% resistance=220 package=THT]
  R3 = Resistor [tolerance=±5% resistance=220 package=THT]
  Part2 = IR Receiver Breakout [package=PCB]

nets:
  N1: Part1.D8, R1.Pin_0
  GND: Part1.GND, Part2.GND
  N2: Part1.D3_PWM, Part2.OUT
  N3: Part1.D6_PWM, R3.Pin_0
  N4: Part1.D7, R2.Pin_0
  5V: Part1.5V, LED1.common_anode, Part2.VCC
  N5: LED1.red_cathode, R3.Pin_1
  N6: LED1.blue_cathode, R2.Pin_1
  N7: LED1.green_cathode, R1.Pin_1
