# Fritzing sketch mcp23017 and 8 leds (saved by Fritzing 0.9.2b)

parts:
  IC1 = MCP23017 I2C I/O Expander
  R1 = Resistor [tolerance=±5% resistance=470 package=THT]
  LED1 = LED - 5mm [color="Red (633nm)" package="5 mm [THT]"]
  R2 = Resistor [tolerance=±5% resistance=470 package=THT]
  LED2 = LED - 5mm [color="Red (633nm)" package="5 mm [THT]"]
  R3 = Resistor [tolerance=±5% resistance=470 package=THT]
  R4 = Resistor [tolerance=±5% resistance=470 package=THT]
  LED3 = LED - 5mm [color="Red (633nm)" package="5 mm [THT]"]
  LED4 = LED - 5mm [color="Red (633nm)" package="5 mm [THT]"]
  R5 = Resistor [tolerance=±5% resistance=470 package=THT]
  R6 = Resistor [tolerance=±5% resistance=470 package=THT]
  R7 = Resistor [tolerance=±5% resistance=470 package=THT]
  R8 = Resistor [tolerance=±5% resistance=470 package=THT]
  LED5 = LED - 5mm [color="Red (633nm)" package="5 mm [THT]"]
  LED6 = LED - 5mm [color="Red (633nm)" package="5 mm [THT]"]
  LED7 = LED - 5mm [color="Red (633nm)" package="5 mm [THT]"]
  LED8 = LED - 5mm [color="Red (633nm)" package="5 mm [THT]"]

nets:
  5V: IC1.VDD, IC1.RESET
  GND: IC1.VSS, IC1.A0, LED1.cathode, LED2.cathode, LED3.cathode, LED4.cathode, LED5.cathode, LED6.cathode, LED7.cathode, LED8.cathode
  ARDUINO A5: IC1.SCL
  ARDUINO A4: IC1.SDA
  N1: IC1.A1, IC1.A2
  N2: IC1.GPA0, R1.Pin_0
  N3: IC1.GPA1, R2.Pin_0
  N4: IC1.GPA2, R4.Pin_0
  N5: IC1.GPA3, R3.Pin_0
  N6: IC1.GPA4, R8.Pin_0
  N7: IC1.GPA5, R6.Pin_0
  N8: IC1.GPA6, R7.Pin_0
  N9: IC1.GPA7, R5.Pin_0
  N10: R1.Pin_1, LED1.anode
  N11: R2.Pin_1, LED2.anode
  N12: R3.Pin_1, LED4.anode
  N13: R4.Pin_1, LED3.anode
  N14: R5.Pin_1, LED6.anode
  N15: R6.Pin_1, LED7.anode
  N16: R7.Pin_1, LED8.anode
  N17: R8.Pin_1, LED5.anode

custom parts:
  MCP23017 I2C I/O Expander: MCP23017 I2C 16-Channel I/O Expander
