# Fritzing sketch arduino 7 segment (saved by Fritzing 0.9.0b)
breadboards: 1

parts:
  Part1 = Arduino Uno (Rev3)
  7_Segment1 = 7 Segment Display

nets:
  N1: Part1.D8, 7_Segment1.Segment_E
  N2: Part1.D9_PWM, 7_Segment1.Segment_F
  N3: Part1.D10_PWM/SS, 7_Segment1.Segment_G
  N4: Part1.D4, 7_Segment1.Segment_A
  N5: Part1.D5_PWM, 7_Segment1.Segment_B
  N6: Part1.D6_PWM, 7_Segment1.Segment_C
  N7: Part1.D7, 7_Segment1.Segment_D
  5V: 7_Segment1.common_anode
