# Fritzing sketch arduino and TM1638 (saved by Fritzing 0.9.0b)

parts:
  Part1 = Arduino Uno (Rev3)
  J1 = female pin header, 5 pins [form="♀ (female)"]

nets:
  N1: Part1.D8, J1.pin5
  N2: Part1.D9_PWM, J1.pin4
  N3: Part1.D10_PWM/SS, J1.pin3
  N4: Part1.GND, J1.pin2
  N5: Part1.5V, J1.pin1

notes:
  Pinout
  1 - VCC
  2 - GND
  3 - STB
  4 - CLK
  5 - DIO
