# Fritzing sketch arduino button (saved by Fritzing 0.9.0b)
breadboards: 1

parts:
  Part1 = Arduino Uno (Rev3)
  R1 = Resistor [tolerance=±5% resistance=1k package=THT]
  R2 = Resistor [tolerance=±5% resistance=1k package=THT]
  S1 = Pushbutton [package="[THT]"]

nets (from the schematic view):
  N1: Part1.D3_PWM, R1.Pin_1
  N2: Part1.5V, R2.Pin_0
  N3: Part1.GND, S1.Pin_3, S1.Pin_4
  N4: R1.Pin_0, R2.Pin_1, S1.Pin_1, S1.Pin_2
