# Fritzing sketch arduin and keypad (saved by Fritzing 0.9.0b)

parts:
  KEYPAD1 = Membrane Matrix Keypad
  Part1 = Arduino Uno (Rev3)

nets:
  N1: KEYPAD1.1, Part1.D8
  N2: KEYPAD1.2, Part1.D7
  N3: KEYPAD1.3, Part1.D6_PWM
  N4: KEYPAD1.4, Part1.D5_PWM
  N5: KEYPAD1.5, Part1.D4
  N6: KEYPAD1.6, Part1.D3_PWM
  N7: KEYPAD1.7, Part1.D2

custom parts:
  Membrane Matrix Keypad: Membrane Matrix 3x4 Keypad
