# Fritzing sketch ardion speaker (saved by Fritzing 0.9.0b)

parts:
  Part1 = Arduino Uno (Rev3)
  R1 = Resistor [tolerance=±5% resistance=100 package=THT]
  SPKR1 = Loudspeaker

nets:
  N1: Part1.GND, SPKR1.pin1
  N2: Part1.D3_PWM, R1.Pin_0
  N3: R1.Pin_1, SPKR1.pin2
