# Fritzing sketch arduino and ttp224 (saved by Fritzing 0.9.0b)
breadboards: 1

parts:
  Part1 = Arduino Uno (Rev3)
  CAP_connection = Header 6 [package=molex-1x6-ra_lock]

nets:
  N1: Part1.D4, CAP_connection.5
  N2: Part1.D5_PWM, CAP_connection.1
  N3: Part1.D6_PWM, CAP_connection.6
  N4: Part1.D7, CAP_connection.2
  GND: CAP_connection.3
  5V: CAP_connection.4

notes:
  1 : OUT1
  2 : OUT2
  3 : OUT3
  4 : OUT4
  5 : GND
  6 : VCC
