# Fritzing sketch arduinocapacitance (saved by Fritzing 0.9.2b)
breadboards: 1

parts:
  Part1 = Arduino Uno (Rev3)
  R1 = Resistor [tolerance=±5% resistance=10k package=THT]
  R2 = Resistor [tolerance=±5% resistance=220 package=THT]
  C1 = Electrolytic Capacitor [capacitance=1µF package="100 mil [THT, electrolytic]"]

nets:
  N1: Part1.A0, R1.Pin_1, R2.Pin_0, C1.+
  N2: Part1.D11_PWM/MOSI, R2.Pin_1
  N3: Part1.D13/SCK, R1.Pin_0
  N4: Part1.GND, C1.-
