# Fritzing sketch Nano_RGBLED (saved by Fritzing 0.9.0b)
breadboards: 1

parts:
  LED1 = RGB LED (com. cathode, rgb) [package="5 mm [THT]"]
  Part1 = Arduino Nano (Rev3.0)

nets:
  N1: LED1.red_anode, Part1.D7
  5V: LED1.common_cathode
  N2: LED1.green_anode, Part1.D5
  N3: LED1.blue_anode, Part1.D6

notes:
  Arduino Nano RGB examples, a
