# Fritzing sketch arduino pwm led (saved by Fritzing 0.9.0b)
breadboards: 1

parts:
  Part1 = Arduino Uno (Rev3)
  R1 = Resistor [tolerance=±5% resistance=10k package=THT]
  R2 = Photocell (LDR) [package=THT]
  R3 = Resistor [tolerance=±5% resistance=220 package=THT]
  LED1 = LED - 5mm [color="Red (633nm)" package="5 mm [THT]"]

nets:
  N1: Part1.D9_PWM, R3.Pin_0
  N2: R1.Pin_0, R2.pin_1
  GND: R1.Pin_1, LED1.cathode
  5V: R2.pin_0
  N3: R3.Pin_1, LED1.anode
